# Fritzing sketch Part 16 Circuit - Simon Says (saved by Fritzing 0.9.2b)
breadboards: 1

parts:
  Part1 = Arduino Uno (Rev3) - ICSP
  S1 = Pushbutton [package="[THT]"]
  S2 = Pushbutton [package="[THT]"]
  S3 = Pushbutton [package="[THT]"]
  S4 = Pushbutton [package="[THT]"]
  LED5 = LED - 5mm [color="Yellow (585nm)" package="5 mm [THT]"]
  LED6 = LED - 5mm [color="Green (555nm)" package="5 mm [THT]"]
  LED7 = LED - 5mm [color="Blue (430nm)" package="5 mm [THT]"]
  J1 = Piezo Speaker
  R1 = Resistor [tolerance=±5% resistance=330 package=THT]
  R2 = Resistor [tolerance=±5% resistance=330 package=THT]
  R3 = Resistor [tolerance=±5% resistance=330 package=THT]
  R4 = Resistor [tolerance=±5% resistance=330 package=THT]
  LED8 = LED - 5mm [color="Red (633nm)" package="5 mm [THT]"]

nets:
  N1: Part1.D8, J1.pin2
  N2: Part1.D9_PWM, J1.pin1
  N3: Part1.D10_PWM/SS, R2.Pin_0
  N4: Part1.D11_PWM/MOSI, S4.Pin_1, S4.Pin_2
  N5: Part1.D12/MISO, S3.Pin_3, S3.Pin_4
  N6: Part1.D13/SCK, R1.Pin_0
  N7: Part1.D2, R4.Pin_0
  N8: Part1.D3_PWM, S2.Pin_3, S2.Pin_4
  N9: Part1.D4, S1.Pin_1, S1.Pin_2
  N10: Part1.D5_PWM, R3.Pin_0
  N11: Part1.GND, S1.Pin_3, S1.Pin_4, S2.Pin_1, S2.Pin_2, S3.Pin_1, S3.Pin_2, S4.Pin_3, S4.Pin_4, LED5.cathode, LED6.cathode, LED7.cathode, LED8.cathode
  N12: LED5.anode, R1.Pin_1
  N13: LED6.anode, R3.Pin_1
  N14: LED7.anode, R2.Pin_1
  N15: R4.Pin_1, LED8.anode
