# Fritzing sketch Part 2 Circuit - Reading a Pot (saved by Fritzing 0.9.2b)
breadboards: 1

parts:
  Part1 = Arduino Uno (Rev3) - ICSP
  R1 = Resistor [tolerance=±5% resistance=330 package="1206 [SMD]"]
  POT1 = Breadboard Trimpot
  LED1 = LED - 5mm [color="Red (633nm)" package="5 mm [THT]"]

nets:
  N1: Part1.A0, POT1.PIN2
  N2: Part1.D13/SCK, LED1.anode
  N3: Part1.5V, POT1.PIN1
  N4: Part1.GND, R1.Pin_0, POT1.PIN3
  N5: R1.Pin_1, LED1.cathode
