# Fritzing sketch Part 5 Circuit - Push Buttons (saved by Fritzing 0.9.3b)
breadboards: 1

parts:
  Part1 = Arduino Uno (Rev3) - ICSP
  LED4 = LED - 5mm [color="Red (635nm)" package="5 mm [THT]"]
  R1 = Resistor [tolerance=±5% resistance=330 package=THT]
  S1 = Pushbutton [package="[THT]"]
  S2 = Pushbutton [package="[THT]"]
  R3 = Resistor [tolerance=±5% resistance=10k package=THT]
  R2 = Resistor [tolerance=±5% resistance=10k package=THT]

nets:
  N1: Part1.D9_PWM, LED4.anode
  N2: Part1.D2, S2.Pin_3, S2.Pin_4, R3.Pin_1
  N3: Part1.D3_PWM, S1.Pin_1, S1.Pin_2, R2.Pin_1
  N4: Part1.5V, R3.Pin_0, R2.Pin_0
  N5: Part1.GND, R1.Pin_0, S1.Pin_3, S1.Pin_4, S2.Pin_1, S2.Pin_2
  N6: LED4.cathode, R1.Pin_1
