# Fritzing sketch Rover_Uno (saved by Fritzing 0.9.3b)

parts:
  Part1 = Arduino Uno (Rev3) - ICSP
  J1 = Basic Servo
  J2 = Basic Servo

nets:
  N1: Part1.D0/RX, J1.pulse
  N2: Part1.D1/TX, J2.pulse
