# Fritzing sketch Part 3 Circuit - RGB LED (saved by Fritzing 0.9.2b)
breadboards: 1

parts:
  Part1 = Arduino Uno (Rev3) - ICSP
  LED4 = RGB LED (com. anode, rbg) [package="5 mm [THT]"]
  R1 = Resistor [tolerance=±5% resistance=330 package="1206 [SMD]"]
  R2 = Resistor [tolerance=±5% resistance=330 package="1206 [SMD]"]
  R3 = Resistor [tolerance=±5% resistance=330 package="1206 [SMD]"]

nets:
  N1: Part1.D9_PWM, R1.Pin_0
  N2: Part1.D10_PWM/SS, R2.Pin_0
  N3: Part1.D11_PWM/MOSI, R3.Pin_0
  N4: Part1.5V, LED4.common_anode
  N5: LED4.red_cathode, R1.Pin_1
  N6: LED4.blue_cathode, R2.Pin_1
  N7: LED4.green_cathode, R3.Pin_1
