# Fritzing sketch Part 4 Circuit - Multiple LEDs (saved by Fritzing 0.9.2b)
breadboards: 1

parts:
  Part1 = Arduino Uno (Rev3) - ICSP
  LED4 = LED - 5mm [color="Red (635nm)" package="5 mm [THT]"]
  LED5 = LED - 5mm [color="Yellow (592nm)" package="5 mm [THT]"]
  LED6 = LED - 5mm [color="Green (555nm)" package="5 mm [THT]"]
  LED7 = LED - 5mm [color="Blue (430nm)" package="5 mm [THT]"]
  LED8 = LED - 5mm [color="Red (635nm)" package="5 mm [THT]"]
  LED9 = LED - 5mm [color="Yellow (592nm)" package="5 mm [THT]"]
  LED10 = LED - 5mm [color="Green (555nm)" package="5 mm [THT]"]
  LED11 = LED - 5mm [color="Blue (430nm)" package="5 mm [THT]"]
  R1 = Resistor [tolerance=±5% resistance=330 package=THT]
  R2 = Resistor [tolerance=±5% resistance=330 package=THT]
  R3 = Resistor [tolerance=±5% resistance=330 package=THT]
  R4 = Resistor [tolerance=±5% resistance=330 package=THT]
  R5 = Resistor [tolerance=±5% resistance=330 package=THT]
  R6 = Resistor [tolerance=±5% resistance=330 package=THT]
  R7 = Resistor [tolerance=±5% resistance=330 package=THT]
  R8 = Resistor [tolerance=±5% resistance=330 package=THT]

nets:
  N1: Part1.D8, LED5.anode
  N2: Part1.D9_PWM, LED4.anode
  N3: Part1.D2, LED11.anode
  N4: Part1.D3_PWM, LED10.anode
  N5: Part1.D4, LED9.anode
  N6: Part1.D5_PWM, LED8.anode
  N7: Part1.D6_PWM, LED7.anode
  N8: Part1.D7, LED6.anode
  N9: Part1.GND, R1.Pin_0, R2.Pin_0, R3.Pin_0, R4.Pin_0, R5.Pin_0, R6.Pin_0, R7.Pin_0, R8.Pin_0
  N10: LED4.cathode, R1.Pin_1
  N11: LED5.cathode, R2.Pin_1
  N12: LED6.cathode, R3.Pin_1
  N13: LED7.cathode, R4.Pin_1
  N14: LED8.cathode, R5.Pin_1
  N15: LED9.cathode, R6.Pin_1
  N16: LED10.cathode, R7.Pin_1
  N17: LED11.cathode, R8.Pin_1
