# Fritzing sketch Part 6 Circuit - NightLight (saved by Fritzing 0.9.2b)
breadboards: 1

parts:
  Part1 = Arduino Uno (Rev3) - ICSP
  LED4 = LED - 5mm [color="Red (635nm)" package="5 mm [THT]"]
  R1 = Resistor [tolerance=±5% resistance=330 package=THT]
  R3 = Resistor [tolerance=±5% resistance=10k package=THT]
  R4 = Photocell (LDR) [package=THT]

nets:
  N1: Part1.A0, R3.Pin_1, R4.pin_0
  N2: Part1.D9_PWM, LED4.anode
  N3: Part1.5V, R4.pin_1
  N4: Part1.GND, R1.Pin_0, R3.Pin_0
  N5: LED4.cathode, R1.Pin_1
