# Fritzing sketch Part 9 Circuit - Servo Knob (saved by Fritzing 0.9.3b)
breadboards: 1

parts:
  Part1 = Arduino Uno (Rev3) - ICSP
  POT1 = Breadboard Trimpot
  J1 = Basic Servo

nets:
  N1: Part1.A0, POT1.PIN2
  N2: Part1.D9_PWM, J1.pulse
  5V: Part1.5V, POT1.PIN1, J1.vcc
  GND: Part1.GND, POT1.PIN3, J1.gnd
